// Logisim project TOY8.circ as structural Verilog: 26 circuits, main circuit OR_gate
module OR_gate (
  input  in_1,
  input  in_2,
  output out_3
);

  wire transistor_1_out, transistor_2_out;

  Transistor transistor_1 (.in(1'b1), .out(transistor_1_out), .gate(in_1));
  Transistor transistor_2 (.in(transistor_1_out), .out(transistor_2_out), .gate(in_2));
  Transistor #(.\type ("n")) transistor_3 (.in(1'b0), .out(transistor_2_out), .gate(in_1));
  Transistor #(.\type ("n")) transistor_4 (.in(1'b0), .out(transistor_2_out), .gate(in_2));
  NOT_gate not_gate_1 (.x(transistor_2_out), .y(out_3));
endmodule

module NOT_gate (
  input  x,
  output y
);

  Transistor transistor_1 (.in(1'b1), .out(y), .gate(x));
  Transistor #(.\type ("n")) transistor_2 (.in(1'b0), .out(y), .gate(x));
endmodule

module NAND_gate (
  input  in_1,
  input  in_2,
  output out_3
);

  wire transistor_2_out;

  Pull_Resistor #(.pull(1)) pull_resistor_1 (.node(out_3));
  Transistor #(.\type ("n")) transistor_1 (.in(transistor_2_out), .out(out_3), .gate(in_1));
  Transistor #(.\type ("n")) transistor_2 (.in(1'b0), .out(transistor_2_out), .gate(in_2));
endmodule

module NOR_gate (
  input  in_1,
  input  in_2,
  output out_3
);

  Pull_Resistor #(.pull(1)) pull_resistor_1 (.node(out_3));
  Transistor #(.\type ("n")) transistor_1 (.in(1'b0), .out(out_3), .gate(in_1));
  Transistor #(.\type ("n")) transistor_2 (.in(1'b0), .out(out_3), .gate(in_2));
endmodule

module XOR_gate (
  input  in_1,
  input  in_2,
  output out_3
);

  wire pull_resistor_2_node, transistor_2_out;

  Pull_Resistor #(.pull(1)) pull_resistor_1 (.node(out_3));
  Transistor #(.\type ("n")) transistor_1 (.in(transistor_2_out), .out(out_3), .gate(in_1));
  Transistor #(.\type ("n")) transistor_2 (.in(1'b0), .out(transistor_2_out), .gate(in_2));
  Pull_Resistor #(.pull(1)) pull_resistor_2 (.node(pull_resistor_2_node));
  Transistor #(.\type ("n")) transistor_3 (.in(1'b0), .out(pull_resistor_2_node), .gate(in_2));
  Transistor #(.\type ("n")) transistor_4 (.in(1'b0), .out(pull_resistor_2_node), .gate(in_1));
  Pull_Resistor #(.pull(1)) pull_resistor_3 (.node(out_3));
  Transistor #(.\type ("n")) transistor_5 (.in(1'b0), .out(out_3), .gate(pull_resistor_2_node));
endmodule

module AND_gate (
  input  in_1,
  input  in_2,
  output out_3
);

  wire nand_gate_1_out_3;

  NAND_gate nand_gate_1 (.in_1(in_1), .in_2(in_2), .out_3(nand_gate_1_out_3));
  NOT_gate not_gate_1 (.x(nand_gate_1_out_3), .y(out_3));
endmodule

module XNOR_gate (
  input  in_1,
  input  in_2,
  output out_3
);

  wire xor_gate_1_out_3;

  XOR_gate xor_gate_1 (.in_1(in_1), .in_2(in_2), .out_3(xor_gate_1_out_3));
  NOT_gate not_gate_1 (.x(xor_gate_1_out_3), .y(out_3));
endmodule

module three_input_AND_gate (
  input  in_1,
  input  in_2,
  input  in_3,
  output out_4
);

  wire pull_resistor_1_node, transistor_2_out, transistor_3_out;

  Pull_Resistor #(.pull(1)) pull_resistor_1 (.node(pull_resistor_1_node));
  Transistor #(.\type ("n")) transistor_1 (.in(transistor_2_out), .out(pull_resistor_1_node), .gate(in_1));
  Transistor #(.\type ("n")) transistor_2 (.in(transistor_3_out), .out(transistor_2_out), .gate(in_2));
  Transistor #(.\type ("n")) transistor_3 (.in(1'b0), .out(transistor_3_out), .gate(in_3));
  NOT_gate not_gate_1 (.x(pull_resistor_1_node), .y(out_4));
endmodule

module multi_input_OR_gate (
  input  in_1,
  input  in_2,
  input  in_3,
  output out_4
);

  wire pull_resistor_1_node, transistor_2_out, transistor_3_out;

  Pull_Resistor pull_resistor_1 (.node(pull_resistor_1_node));
  Transistor transistor_1 (.in(transistor_2_out), .out(pull_resistor_1_node), .gate(in_1));
  Transistor transistor_2 (.in(transistor_3_out), .out(transistor_2_out), .gate(in_2));
  Transistor transistor_3 (.in(1'b1), .out(transistor_3_out), .gate(in_3));
  NOT_gate not_gate_1 (.x(pull_resistor_1_node), .y(out_4));
endmodule

module half_adder (
  input  a,
  input  b,
  output sum,
  output carry
);

  XOR_gate xor_gate_1 (.in_1(a), .in_2(b), .out_3(sum));
  AND_gate and_gate_1 (.in_1(a), .in_2(b), .out_3(carry));
endmodule

module ODD (
  input  a,
  input  b,
  input  c,
  output out_4
);

  wire xor_1_out, xor_2_out;

  xor xor_1 (xor_1_out, a, b);
  xor xor_2 (xor_2_out, xor_1_out, c);
  not not_1 (out_4, xor_2_out);
endmodule

module MAJ (
  input  a,
  input  b,
  input  c,
  output z
);

  wire and_1_out, and_2_out, and_3_out;

  and and_1 (and_1_out, c, b);
  and and_2 (and_2_out, b, a);
  and and_3 (and_3_out, c, a);
  or or_1 (z, and_1_out, and_2_out, and_3_out);
endmodule

module full_adder (
  input  a,
  input  b,
  input  cin,
  output sum,
  output cout
);

  wire odd_1_out_4;

  ODD odd_1 (.a(a), .b(b), .c(cin), .out_4(odd_1_out_4));
  MAJ maj_1 (.a(a), .b(b), .c(cin), .z(cout));
  not not_1 (sum, odd_1_out_4);
endmodule

module eight_bit_ripple_carry_adder (
  input  [7:0] a,
  input  Cin,
  input  [7:0] b,
  output [7:0] out_4,
  output out_5
);

  wire full_adder_1_cout, full_adder_2_cout, full_adder_3_cout, full_adder_4_cout, full_adder_5_cout,
       full_adder_6_cout, full_adder_7_cout;

  full_adder full_adder_1 (.a(a[0]), .b(b[0]), .cin(Cin), .sum(out_4[0]), .cout(full_adder_1_cout));
  full_adder full_adder_2 (.a(a[1]), .b(b[1]), .cin(full_adder_1_cout), .sum(out_4[1]), .cout(full_adder_2_cout));
  full_adder full_adder_3 (.a(a[2]), .b(b[2]), .cin(full_adder_2_cout), .sum(out_4[2]), .cout(full_adder_3_cout));
  full_adder full_adder_4 (.a(a[3]), .b(b[3]), .cin(full_adder_3_cout), .sum(out_4[3]), .cout(full_adder_4_cout));
  full_adder full_adder_5 (.a(a[4]), .b(b[4]), .cin(full_adder_4_cout), .sum(out_4[4]), .cout(full_adder_5_cout));
  full_adder full_adder_6 (.a(a[5]), .b(b[5]), .cin(full_adder_5_cout), .sum(out_4[5]), .cout(full_adder_6_cout));
  full_adder full_adder_7 (.a(a[6]), .b(b[6]), .cin(full_adder_6_cout), .sum(out_4[6]), .cout(full_adder_7_cout));
  full_adder full_adder_8 (.a(a[7]), .b(b[7]), .cin(full_adder_7_cout), .sum(out_4[7]), .cout(out_5));
endmodule

module eight_bit_AND_gate (
  input  [7:0] in_1,
  input  [7:0] in_2,
  output [7:0] out_3
);

  AND_gate and_gate_1 (.in_1(in_1[0]), .in_2(in_2[0]), .out_3(out_3[0]));
  AND_gate and_gate_2 (.in_1(in_1[1]), .in_2(in_2[1]), .out_3(out_3[1]));
  AND_gate and_gate_3 (.in_1(in_1[2]), .in_2(in_2[2]), .out_3(out_3[2]));
  AND_gate and_gate_4 (.in_1(in_1[3]), .in_2(in_2[3]), .out_3(out_3[3]));
  AND_gate and_gate_5 (.in_1(in_1[4]), .in_2(in_2[4]), .out_3(out_3[4]));
  AND_gate and_gate_6 (.in_1(in_1[5]), .in_2(in_2[5]), .out_3(out_3[5]));
  AND_gate and_gate_7 (.in_1(in_1[6]), .in_2(in_2[6]), .out_3(out_3[6]));
  AND_gate and_gate_8 (.in_1(in_1[7]), .in_2(in_2[7]), .out_3(out_3[7]));
endmodule

module eight_bit_XOR_gate (
  input  [7:0] in_1,
  input  [7:0] in_2,
  output [7:0] out_3
);

  XOR_gate xor_gate_1 (.in_1(in_1[0]), .in_2(in_2[0]), .out_3(out_3[0]));
  XOR_gate xor_gate_2 (.in_1(in_1[1]), .in_2(in_2[1]), .out_3(out_3[1]));
  XOR_gate xor_gate_3 (.in_1(in_1[2]), .in_2(in_2[2]), .out_3(out_3[2]));
  XOR_gate xor_gate_4 (.in_1(in_1[3]), .in_2(in_2[3]), .out_3(out_3[3]));
  XOR_gate xor_gate_5 (.in_1(in_1[4]), .in_2(in_2[4]), .out_3(out_3[4]));
  XOR_gate xor_gate_6 (.in_1(in_1[5]), .in_2(in_2[5]), .out_3(out_3[5]));
  XOR_gate xor_gate_7 (.in_1(in_1[6]), .in_2(in_2[6]), .out_3(out_3[6]));
  XOR_gate xor_gate_8 (.in_1(in_1[7]), .in_2(in_2[7]), .out_3(out_3[7]));
endmodule

module de_coder (
  input  a,
  input  b,
  input  c,
  input  enable,
  output d1,
  output d2,
  output d3,
  output d4,
  output d5,
  output d6,
  output d7,
  output d8
);

  wire not_1_out, not_2_out, not_3_out;

  not not_1 (not_1_out, a);
  not not_2 (not_2_out, b);
  not not_3 (not_3_out, c);
  and and_1 (d1, enable, not_1_out, not_2_out, not_3_out);
  and and_2 (d2, enable, not_1_out, not_2_out, c);
  and and_3 (d3, enable, not_1_out, b, not_3_out);
  and and_4 (d4, enable, not_1_out, b, c);
  and and_5 (d5, enable, a, not_2_out, not_3_out);
  and and_6 (d6, enable, a, not_2_out, c);
  and and_7 (d7, enable, a, b, not_3_out);
  and and_8 (d8, enable, a, b, c);
endmodule

module DEMUX (
  input  a,
  input  b,
  input  c,
  input  D,
  output O1,
  output O2,
  output O3,
  output O4,
  output O5,
  output O6,
  output O7,
  output O8
);

  wire de_coder_1_d1, de_coder_1_d2, de_coder_1_d3, de_coder_1_d4, de_coder_1_d5, de_coder_1_d6,
       de_coder_1_d7, de_coder_1_d8;

  de_coder de_coder_1 (
    .a(a), .b(b), .c(c), .enable(1'b1), .d1(de_coder_1_d1), .d2(de_coder_1_d2), .d3(de_coder_1_d3),
    .d4(de_coder_1_d4), .d5(de_coder_1_d5), .d6(de_coder_1_d6), .d7(de_coder_1_d7), .d8(de_coder_1_d8));
  and and_1 (O1, de_coder_1_d1, D);
  and and_2 (O2, de_coder_1_d2, D);
  and and_3 (O3, de_coder_1_d3, D);
  and and_4 (O4, de_coder_1_d4, D);
  and and_5 (O5, de_coder_1_d5, D);
  and and_6 (O6, de_coder_1_d6, D);
  and and_7 (O7, de_coder_1_d7, D);
  and and_8 (O8, de_coder_1_d8, D);
endmodule

module decoder_demux (
  input  a,
  input  b,
  input  c,
  input  [3:0] D,
  output [3:0] D1,
  output out_6,
  output [3:0] D2,
  output out_8,
  output [3:0] D3,
  output out_10,
  output [3:0] D4,
  output out_12,
  output [3:0] D5,
  output out_14,
  output [3:0] D6,
  output out_16,
  output [3:0] D7,
  output out_18,
  output [3:0] D8,
  output out_20
);

  wire not_1_out, not_2_out, not_3_out;

  not not_1 (not_1_out, a);
  not not_2 (not_2_out, b);
  not not_3 (not_3_out, c);
  and and_1 (out_6, not_1_out, not_2_out, not_3_out);
  and and_2 (out_8, not_1_out, not_2_out, c);
  and and_3 (out_10, not_1_out, b, not_3_out);
  and and_4 (out_12, not_1_out, b, c);
  and and_5 (out_14, a, not_2_out, not_3_out);
  and and_6 (out_16, a, not_2_out, c);
  and and_7 (out_18, a, b, not_3_out);
  and and_8 (out_20, a, b, c);
  Pull_Resistor pull_resistor_1 (.node(D1));
  assign D1 = out_6 ? D : 4'bz;  // Controlled_Buffer controlled_buffer_1
  Pull_Resistor pull_resistor_2 (.node(D2));
  assign D2 = out_8 ? D : 4'bz;  // Controlled_Buffer controlled_buffer_2
  Pull_Resistor pull_resistor_3 (.node(D3));
  assign D3 = out_10 ? D : 4'bz;  // Controlled_Buffer controlled_buffer_3
  Pull_Resistor pull_resistor_4 (.node(D4));
  assign D4 = out_12 ? D : 4'bz;  // Controlled_Buffer controlled_buffer_4
  Pull_Resistor pull_resistor_5 (.node(D5));
  assign D5 = out_14 ? D : 4'bz;  // Controlled_Buffer controlled_buffer_5
  Pull_Resistor pull_resistor_6 (.node(D6));
  assign D6 = out_16 ? D : 4'bz;  // Controlled_Buffer controlled_buffer_6
  Pull_Resistor pull_resistor_7 (.node(D7));
  assign D7 = out_18 ? D : 4'bz;  // Controlled_Buffer controlled_buffer_7
  Pull_Resistor pull_resistor_8 (.node(D8));
  assign D8 = out_20 ? D : 4'bz;  // Controlled_Buffer controlled_buffer_8
endmodule

module right_bitshifter (
  input  [7:0] in_1,
  output [7:0] out_2
);

  Pull_Resistor pull_resistor_1 (.node(out_2[7]));

  assign out_2[6:0] = in_1[7:1];
endmodule

module left_bitshifter (
  input  [7:0] in_1,
  output [7:0] out_2
);

  Pull_Resistor pull_resistor_1 (.node(out_2[0]));

  assign out_2[7:1] = in_1[6:0];
endmodule

module one_hot_mux_eightbit (
  input  [7:0] add,
  input  [7:0] XORR,
  input  [7:0] andg,
  input  [7:0] subtractor,
  input  [7:0] right_shift,
  input  [7:0] left_shift,
  input  C_ADD,
  input  C_xor,
  input  C_andg,
  input  C_sub,
  input  C_RS,
  input  C_LS,
  output [7:0] out_13
);

  wire [7:0] eight_bit_and_gate_1_out_3, eight_bit_and_gate_2_out_3, eight_bit_and_gate_3_out_3,
       eight_bit_and_gate_4_out_3, eight_bit_and_gate_5_out_3, eight_bit_and_gate_6_out_3, or_1_out, or_2_out;

  eight_bit_AND_gate eight_bit_and_gate_1 (.in_1(add), .in_2({8{C_ADD}}), .out_3(eight_bit_and_gate_1_out_3));
  eight_bit_AND_gate eight_bit_and_gate_2 (.in_1(XORR), .in_2({8{C_xor}}), .out_3(eight_bit_and_gate_2_out_3));
  eight_bit_AND_gate eight_bit_and_gate_3 (.in_1(andg), .in_2({8{C_andg}}), .out_3(eight_bit_and_gate_3_out_3));
  eight_bit_AND_gate eight_bit_and_gate_4 (.in_1(subtractor), .in_2({8{C_sub}}), .out_3(eight_bit_and_gate_4_out_3));
  eight_bit_AND_gate eight_bit_and_gate_5 (.in_1(right_shift), .in_2({8{C_RS}}), .out_3(eight_bit_and_gate_5_out_3));
  eight_bit_AND_gate eight_bit_and_gate_6 (.in_1(left_shift), .in_2({8{C_LS}}), .out_3(eight_bit_and_gate_6_out_3));
  assign or_1_out = eight_bit_and_gate_1_out_3 | eight_bit_and_gate_2_out_3 | eight_bit_and_gate_3_out_3;  // OR_Gate or_1, 8 bits wide
  assign or_2_out = eight_bit_and_gate_4_out_3 | eight_bit_and_gate_5_out_3 | eight_bit_and_gate_6_out_3;  // OR_Gate or_2, 8 bits wide
  assign out_13 = or_1_out | or_2_out;  // OR_Gate or_3, 8 bits wide
endmodule

module subtractor_1bit (
  input  a,
  input  b,
  input  cin,
  output sum,
  output cout
);

  wire and_1_out, and_2_out, not_1_out, not_2_out, xor_1_out;

  xor xor_1 (xor_1_out, a, b);
  not not_1 (not_1_out, a);
  and and_1 (and_1_out, not_1_out, b);
  xor xor_2 (sum, xor_1_out, cin);
  not not_2 (not_2_out, xor_1_out);
  and and_2 (and_2_out, not_2_out, cin);
  or or_1 (cout, and_1_out, and_2_out);
endmodule

module eight_bit_subtractor (
  input  [7:0] a,
  input  Cin,
  input  [7:0] b,
  output [7:0] out_4,
  output out_5
);

  wire subtractor_1bit_1_cout, subtractor_1bit_2_cout, subtractor_1bit_3_cout, subtractor_1bit_4_cout,
       subtractor_1bit_5_cout, subtractor_1bit_6_cout, subtractor_1bit_7_cout;

  subtractor_1bit subtractor_1bit_1 (.a(a[0]), .b(b[0]), .cin(Cin), .sum(out_4[0]), .cout(subtractor_1bit_1_cout));
  subtractor_1bit subtractor_1bit_2 (
    .a(a[1]), .b(b[1]), .cin(subtractor_1bit_1_cout), .sum(out_4[1]), .cout(subtractor_1bit_2_cout));
  subtractor_1bit subtractor_1bit_3 (
    .a(a[2]), .b(b[2]), .cin(subtractor_1bit_2_cout), .sum(out_4[2]), .cout(subtractor_1bit_3_cout));
  subtractor_1bit subtractor_1bit_4 (
    .a(a[3]), .b(b[3]), .cin(subtractor_1bit_3_cout), .sum(out_4[3]), .cout(subtractor_1bit_4_cout));
  subtractor_1bit subtractor_1bit_5 (
    .a(a[4]), .b(b[4]), .cin(subtractor_1bit_4_cout), .sum(out_4[4]), .cout(subtractor_1bit_5_cout));
  subtractor_1bit subtractor_1bit_6 (
    .a(a[5]), .b(b[5]), .cin(subtractor_1bit_5_cout), .sum(out_4[5]), .cout(subtractor_1bit_6_cout));
  subtractor_1bit subtractor_1bit_7 (
    .a(a[6]), .b(b[6]), .cin(subtractor_1bit_6_cout), .sum(out_4[6]), .cout(subtractor_1bit_7_cout));
  subtractor_1bit subtractor_1bit_8 (.a(a[7]), .b(b[7]), .cin(subtractor_1bit_7_cout), .sum(out_4[7]), .cout(out_5));
endmodule

module ALU (
  input  [7:0] A,
  input  [7:0] B,
  input  s1,
  input  s2,
  input  s3,
  output [7:0] out_6
);

  wire de_coder_1_d2, de_coder_1_d3, de_coder_1_d4, de_coder_1_d5, de_coder_1_d6, de_coder_1_d7;
  wire [7:0] eight_bit_and_gate_1_out_3, eight_bit_ripple_carry_adder_1_out_4, eight_bit_subtractor_1_out_4,
       eight_bit_xor_gate_1_out_3, left_bitshifter_1_out_2, right_bitshifter_1_out_2;

  eight_bit_ripple_carry_adder eight_bit_ripple_carry_adder_1 (
    .a(A), .Cin(1'b0), .b(B), .out_4(eight_bit_ripple_carry_adder_1_out_4));  // open: out_5
  eight_bit_AND_gate eight_bit_and_gate_1 (.in_1(A), .in_2(B), .out_3(eight_bit_and_gate_1_out_3));
  eight_bit_XOR_gate eight_bit_xor_gate_1 (.in_1(A), .in_2(B), .out_3(eight_bit_xor_gate_1_out_3));
  right_bitshifter right_bitshifter_1 (.in_1(A), .out_2(right_bitshifter_1_out_2));
  left_bitshifter left_bitshifter_1 (.in_1(A), .out_2(left_bitshifter_1_out_2));
  eight_bit_subtractor eight_bit_subtractor_1 (
    .a(A), .Cin(1'b0), .b(B), .out_4(eight_bit_subtractor_1_out_4));  // open: out_5
  de_coder de_coder_1 (
    .a(s1), .b(s2), .c(s3), .enable(1'b1), .d2(de_coder_1_d2), .d3(de_coder_1_d3), .d4(de_coder_1_d4),
    .d5(de_coder_1_d5), .d6(de_coder_1_d6), .d7(de_coder_1_d7));  // open: d1, d8
  one_hot_mux_eightbit one_hot_mux_eightbit_1 (
    .add(eight_bit_ripple_carry_adder_1_out_4), .XORR(eight_bit_xor_gate_1_out_3),
    .andg(eight_bit_and_gate_1_out_3), .subtractor(eight_bit_subtractor_1_out_4),
    .right_shift(right_bitshifter_1_out_2), .left_shift(left_bitshifter_1_out_2), .C_ADD(de_coder_1_d2),
    .C_xor(de_coder_1_d3), .C_andg(de_coder_1_d4), .C_sub(de_coder_1_d5), .C_RS(de_coder_1_d6),
    .C_LS(de_coder_1_d7), .out_13(out_6));
endmodule

module demux_again (
  input  a,
  input  b,
  input  c,
  input  [3:0] D,
  output [3:0] D1,
  output [3:0] D2,
  output [3:0] D3,
  output [3:0] D4,
  output [3:0] D5,
  output [3:0] D6,
  output [3:0] D7,
  output [3:0] D8
);

  wire and_1_out, and_2_out, and_3_out, and_4_out, and_5_out, and_6_out, and_7_out, and_8_out, not_1_out,
       not_2_out, not_3_out;

  not not_1 (not_1_out, a);
  not not_2 (not_2_out, b);
  not not_3 (not_3_out, c);
  and and_1 (and_1_out, not_1_out, not_2_out, not_3_out);
  and and_2 (and_2_out, not_1_out, not_2_out, c);
  and and_3 (and_3_out, not_1_out, b, not_3_out);
  and and_4 (and_4_out, not_1_out, b, c);
  and and_5 (and_5_out, a, not_2_out, not_3_out);
  and and_6 (and_6_out, a, not_2_out, c);
  and and_7 (and_7_out, a, b, not_3_out);
  and and_8 (and_8_out, a, b, c);
  Pull_Resistor pull_resistor_1 (.node(D1));
  assign D1 = and_1_out ? D : 4'bz;  // Controlled_Buffer controlled_buffer_1
  Pull_Resistor pull_resistor_2 (.node(D2));
  assign D2 = and_2_out ? D : 4'bz;  // Controlled_Buffer controlled_buffer_2
  Pull_Resistor pull_resistor_3 (.node(D3));
  assign D3 = and_3_out ? D : 4'bz;  // Controlled_Buffer controlled_buffer_3
  Pull_Resistor pull_resistor_4 (.node(D4));
  assign D4 = and_4_out ? D : 4'bz;  // Controlled_Buffer controlled_buffer_4
  Pull_Resistor pull_resistor_5 (.node(D5));
  assign D5 = and_5_out ? D : 4'bz;  // Controlled_Buffer controlled_buffer_5
  Pull_Resistor pull_resistor_6 (.node(D6));
  assign D6 = and_6_out ? D : 4'bz;  // Controlled_Buffer controlled_buffer_6
  Pull_Resistor pull_resistor_7 (.node(D7));
  assign D7 = and_7_out ? D : 4'bz;  // Controlled_Buffer controlled_buffer_7
  Pull_Resistor pull_resistor_8 (.node(D8));
  assign D8 = and_8_out ? D : 4'bz;  // Controlled_Buffer controlled_buffer_8
endmodule
